# Fritzing sketch wire-diagram (saved by Fritzing 0.9.5d)
breadboards: 1

parts:
  Part1 = Arduino Uno (Rev3) - ICSP  # not connected
  Part2 = adafruit [part_number=931]

nets:
  N1: Part2.connector5, Part2.connector7
